# Fritzing sketch WD (saved by Fritzing 0.9.5d)
breadboards: 1

parts:
  LCD1 = LCD screen
  LCM1602_IIC1 = LCM1602 IIC [part_number="LCM1602 IIC" chip_label="LCM1602 IIC" package="DIP (Dual Inline) [THT]"]
  R1 = Resistor [tolerance=±5% resistance=10000 package="2512 [SMD]"]
  R2 = Resistor [tolerance=±5% resistance=10000 package="1206 [SMD]"]
  R3 = Resistor [tolerance=±5% resistance=10000 package="0402 [SMD]"]
  LED2 = LED - 5mm [color="Red (633nm)" package="5 mm [THT]"]
  LED3 = LED - 5mm [color="Green (555nm)" package="5 mm [THT]"]
  S1 = Pushbutton [package="[SMD]"]
  Mod2 = KY-018 Photoresistor Module [package="Breakout board"]
  WeMos_D1_Mini1 = WeMos D1 Mini
  Mod1 = KY-015 Temperature & Humidity Sensor Module [package="Breakout board"]
  Power_plug1 = USB-C plug  # not connected

nets:
  VSS: LCD1.VSS, LCM1602_IIC1.VSS
  VDD: LCD1.VDD, LCM1602_IIC1.VDD
  N1: LCD1.V0, LCM1602_IIC1.V0
  N2: LCD1.RS, LCM1602_IIC1.RS
  N3: LCD1.R/W, LCM1602_IIC1.RW
  N4: LCD1.E, LCM1602_IIC1.E
  N5: LCD1.DB0, LCM1602_IIC1.D0
  N6: LCD1.DB1, LCM1602_IIC1.D1
  N7: LCD1.DB2, LCM1602_IIC1.D2
  N8: LCD1.DB3, LCM1602_IIC1.D3
  N9: LCD1.DB4, LCM1602_IIC1.D4
  N10: LCD1.DB5, LCM1602_IIC1.D5
  N11: LCD1.DB6, LCM1602_IIC1.D6
  N12: LCD1.DB7, LCM1602_IIC1.D7
  N13: LCD1.LED+, LCM1602_IIC1.A
  N14: LCD1.LED-, LCM1602_IIC1.K
  N15: LCM1602_IIC1.SDA, WeMos_D1_Mini1.D2
  N16: LCM1602_IIC1.SCL, WeMos_D1_Mini1.D1
  N17: R1.Pin_0, S1.Pin_1, S1.Pin_2
  N18: R1.Pin_1, LED2.anode, LED3.anode, Mod1.S
  N19: R2.Pin_1, LED2.cathode
  N20: R3.Pin_1, LED3.cathode
  N21: S1.Pin_3, S1.Pin_4, Mod2.-, Mod1.-

notes:
  LED's
  KY-018
  DHT11
  Liquid crystal display 16 x 2
  Wemos D1 Mini
  USB-C Power Source
  Tactile button
  10k Ohms 1% Resistor

custom parts:
  LCM1602 IIC: I2C-Module to use a 1602 or 2004 LCD on with the wire.h libory Serial LCD Modul
  KY-018 Photoresistor Module: KY-018 Photoresistor module, used to measure light intensity. It can determine the presence or absence of light.
  KY-015 Temperature & Humidity Sensor Module: KY-015 temperature and humidity sensor module, provides a low-latency serial interface to measure humidity and temperature.
  USB-C plug: power plug
